# Fritzing sketch input_pullup (saved by Fritzing 0.9.4)
breadboards: 1

parts:
  Part1 = Arduino Ethernet Shield (Rev3)
  LED1 = LED - 5mm [color="Red (633nm)" package="5 mm [THT]"]
  S1 = Pushbutton [package="[THT]"]
  R1 = Resistor [tolerance=±5% resistance=220 package=THT]

nets:
  N1: Part1.GND, S1.Pin_3, S1.Pin_4, R1.Pin_0
  N2: Part1.D2, LED1.anode
  N3: Part1.SDCS, S1.Pin_1, S1.Pin_2
  N4: LED1.cathode, R1.Pin_1
